# Fritzing sketch plutino (saved by Fritzing 0.9.1b)

parts:
  Arduino1 = Arduino Mini (Rev5)
  J1 = Basic Servo  # not connected
  Composant1 = SRF05 Ultrasonic Rangefinder

nets:
  N1: Arduino1.D11_PWM, Composant1.Echo
  N2: Arduino1.D10_PWM, Composant1.Trig
  GND: Arduino1.GND, Composant1.GND
  5V: Arduino1.5V, Composant1.VCC

notes:
  5V power source
